# Fritzing sketch Armduino (saved by Fritzing 0.9.0b)
breadboards: 1

parts:
  Part1 = Arduino Uno (Rev3)
  IC1 = ULN2803A [package=THT]
  S1 = Pushbutton [package="[SMD]"]
  R1 = Resistor [tolerance=±5% resistance=220 package=THT]
  U1 = Transformer [package=transformer]
  J1 = Power Jack [package=power_jack_pth]
  U2 = W002G Bridge Rectifier [package=THT]
  M2 = Stepper Motor - Unipolar
  M3 = Stepper Motor - Unipolar

nets:
  N1: Part1.D8, IC1.In_4
  N2: Part1.D9_PWM, IC1.In_3
  N3: Part1.D10_PWM/SS, IC1.In_2
  N4: Part1.D11_PWM/MOSI, IC1.In_1
  N5: Part1.GND, IC1.0V, U1.3, U2.Pin_2, U2.Pin_3
  N6: Part1.D3_PWM, S1.Pin_1, S1.Pin_2
  N7: Part1.D4, IC1.In_8
  N8: Part1.D5_PWM, IC1.In_7
  N9: Part1.D6_PWM, IC1.In_6
  N10: Part1.D7, IC1.In_5
  N11: IC1.COM_-_Common, R1.Pin_0, U1.2, U2.Pin_1, U2.Pin_4, M2.C, M2.B, M3.B
  N12: IC1.Out_8, M3.A
  N13: IC1.Out_7, M3.COMMON_2
  N14: IC1.Out_6, M3.COMMON_1
  N15: IC1.Out_5, M3.D
  N16: IC1.Out_4, M2.A
  N17: IC1.Out_3, M2.COMMON_2
  N18: IC1.Out_2, M2.COMMON_1
  N19: IC1.Out_1, M2.D
  N20: S1.Pin_3, S1.Pin_4, R1.Pin_1
  N21: U1.1, J1.PWR
  N22: U1.4, J1.GND

notes:
  12 V AC Transformer
  220 AC
  Pushbutton Not Fully Working for TIP
  First Joint
  Second Joint

custom parts:
  W002G Bridge Rectifier: Converts AC to DC or in another words: creates absolute value of voltage at the input.
